# Fritzing sketch chromeDino (saved by Fritzing 0.8.7b)
breadboards: 1

parts:
  R1 = Photocell (LDR) [package=THT]
  R2 = Resistor [tolerance=±5% resistance=10k package=THT]
  Componente1 = Arduino Uno (Rev3) - ICSP
  J1 = Basic Servo

nets:
  GND: R1.pin_0, Componente1.GND, J1.gnd
  N1: R1.pin_1, R2.Pin_1, Componente1.A5/SCL
  N2: R2.Pin_0, J1.vcc
  N3: Componente1.D6_PWM, J1.pulse
